// Logisim project e_q2_00.circ as structural Verilog: 5 circuits, main circuit main
module main (
  input  [2:0] LEDSTR
);

  wire clock_1_out, counter_3bit_1_out0, counter_3bit_1_out0_2, counter_3bit_1_out1, led_soft_on_1_leout;

  Clock clock_1 (.out(clock_1_out));
  DotMatrix #(.matrixcols(3), .matrixrows(1), .dotshape("circle")) dotmatrix_1 (
    .col0(counter_3bit_1_out0_2), .col1(counter_3bit_1_out1), .col2(counter_3bit_1_out0));
  Counter_3bit counter_3bit_1 (
    .Clk(clock_1_out), .Out0(counter_3bit_1_out0), .Out1(counter_3bit_1_out1), .Out0_2(counter_3bit_1_out0_2));
  LED_Soft_On led_soft_on_1 (.LEOUT(led_soft_on_1_leout), .LEDSTR(LEDSTR), .Clk(clock_1_out));
  LED led_1 (.in(led_soft_on_1_leout));
endmodule

// HA
module Half_Adder (
  input  A,
  input  B,
  output Sum,
  output C
);

  xor xor_1 (Sum, A, B);
  and and_1 (C, A, B);
endmodule

// CNT
module Counter_3bit (
  input  Clk,
  output Out0,
  output Out1,
  output Out0_2
);

  wire and_1_out, d_ff_1_q, d_ff_2_q, d_ff_2_qn, d_ff_3_q, half_adder_1_c, half_adder_1_sum, half_adder_2_c,
       half_adder_2_sum, half_adder_3_sum, not_1_out;

  Half_Adder half_adder_1 (.A(Clk), .B(Out0), .Sum(half_adder_1_sum), .C(half_adder_1_c));
  Half_Adder half_adder_2 (.A(half_adder_1_c), .B(Out1), .Sum(half_adder_2_sum), .C(half_adder_2_c));
  Half_Adder half_adder_3 (.A(half_adder_2_c), .B(Out0_2), .Sum(half_adder_3_sum));  // open: C
  D_Flip_Flop #(.trigger("falling")) d_ff_1 (
    .clk(Clk), .D(half_adder_1_sum), .Q(d_ff_1_q));  // open: Qn, preset, en, reset
  D_Flip_Flop #(.trigger("falling")) d_ff_2 (
    .clk(Clk), .D(half_adder_2_sum), .Q(d_ff_2_q), .Qn(d_ff_2_qn));  // open: preset, en, reset
  D_Flip_Flop #(.trigger("falling")) d_ff_3 (
    .clk(Clk), .D(half_adder_3_sum), .Q(d_ff_3_q));  // open: Qn, preset, en, reset
  and _0 (Out0, d_ff_1_q, not_1_out);
  and and_1 (and_1_out, d_ff_1_q, d_ff_2_qn, d_ff_3_q);
  and _1 (Out1, d_ff_2_q, not_1_out);
  not not_1 (not_1_out, and_1_out);
  and _2 (Out0_2, d_ff_3_q, not_1_out);
endmodule

module Compare_3bit (
  input  A0,
  input  A1,
  input  A2,
  input  B0,
  input  B1,
  input  B2,
  output Out
);

  wire not_1_out, not_2_out, not_3_out, xor_1_out, xor_2_out, xor_3_out;

  xor xor_1 (xor_1_out, A0, B0);
  not not_1 (not_1_out, xor_1_out);
  xor xor_2 (xor_2_out, A1, B1);
  not not_2 (not_2_out, xor_2_out);
  and and_1 (Out, not_1_out, not_2_out, not_3_out);
  xor xor_3 (xor_3_out, A2, B2);
  not not_3 (not_3_out, xor_3_out);
endmodule

module LED_Soft_On (
  input  Clk,
  input  [2:0] LEDSTR,
  output LEOUT
);

  wire and_1_out, and_2_out, compare_3bit_1_out, counter_3bit_1_out0, counter_3bit_1_out0_2,
       counter_3bit_1_out1, d_ff_1_q, not_1_out, not_2_out, not_3_out, not_4_out, xor_1_out;

  Counter_3bit counter_3bit_1 (
    .Clk(Clk), .Out0(counter_3bit_1_out0), .Out1(counter_3bit_1_out1), .Out0_2(counter_3bit_1_out0_2));
  not not_1 (not_1_out, counter_3bit_1_out0);
  not not_2 (not_2_out, counter_3bit_1_out1);
  not not_3 (not_3_out, counter_3bit_1_out0_2);
  and and_1 (and_1_out, not_1_out, not_2_out, not_3_out);
  Compare_3bit compare_3bit_1 (
    .A0(counter_3bit_1_out0), .A1(counter_3bit_1_out1), .A2(counter_3bit_1_out0_2), .B0(LEDSTR[0]),
    .B1(LEDSTR[1]), .B2(LEDSTR[2]), .Out(compare_3bit_1_out));
  not not_4 (not_4_out, LEDSTR[1]);
  ExactlyOne xor_1 (.out(xor_1_out), .in0(compare_3bit_1_out), .in1(and_1_out), .in2(d_ff_1_q));
  and and_2 (and_2_out, LEDSTR[2], not_4_out, LEDSTR[0]);
  D_Flip_Flop #(.trigger("falling")) d_ff_1 (.clk(Clk), .D(xor_1_out), .Q(d_ff_1_q));  // open: Qn, preset, en, reset
  or or_1 (LEOUT, and_2_out, d_ff_1_q);
endmodule
