// Logisim project e_q1_00.circ as structural Verilog: 4 circuits, main circuit main
module main (
);

  wire clock_1_out, q01_05_1_c_prime_0, q01_05_1_c_prime_1, q01_05_1_carry, q01_05_2_c_prime_0,
       q01_05_2_c_prime_1, q01_05_2_carry, q01_05_3_c_prime_0, q01_05_3_c_prime_1;

  Clock clock_1 (.out(clock_1_out));
  q01_05 q01_05_1 (
    .clk(clock_1_out), .en(1'b1), .c_prime_0(q01_05_1_c_prime_0), .c_prime_1(q01_05_1_c_prime_1),
    .carry(q01_05_1_carry));
  q01_05 q01_05_2 (
    .clk(clock_1_out), .en(q01_05_1_carry), .c_prime_0(q01_05_2_c_prime_0), .c_prime_1(q01_05_2_c_prime_1),
    .carry(q01_05_2_carry));
  q01_05 q01_05_3 (
    .clk(clock_1_out), .en(q01_05_2_carry), .c_prime_0(q01_05_3_c_prime_0), .c_prime_1(q01_05_3_c_prime_1));  // open: carry
  LED led_1 (.in(q01_05_1_c_prime_0));
  LED led_2 (.in(q01_05_1_c_prime_1));
  LED led_3 (.in(q01_05_2_c_prime_0));
  LED led_4 (.in(q01_05_2_c_prime_1));
  LED led_5 (.in(q01_05_3_c_prime_0));
  LED led_6 (.in(q01_05_3_c_prime_1));
endmodule

module q01_03 (
  input  clk,
  input  en,
  output c_prime_0,
  output c_prime_1
);

  wire and_1_out, and_2_out, and_3_out, not_1_out, not_2_out, xor_1_out;

  xor xor_1 (xor_1_out, c_prime_0, en);
  and and_1 (and_1_out, xor_1_out, not_1_out);
  not not_1 (not_1_out, c_prime_1);
  not not_2 (not_2_out, c_prime_1);
  and and_2 (and_2_out, not_2_out, c_prime_0);
  and and_3 (and_3_out, and_2_out, en);
  D_Flip_Flop d_ff_1 (.clk(clk), .D(and_1_out), .Q(c_prime_0));  // open: Qn, preset, en, reset
  D_Flip_Flop d_ff_2 (.clk(clk), .D(and_3_out), .Q(c_prime_1));  // open: Qn, preset, en, reset
endmodule

module q01_04 (
  input  clk,
  input  en,
  output c_prime_0,
  output c_prime_1
);

  wire and_1_out, and_2_out, and_3_out, and_4_out, and_5_out, not_1_out, not_2_out, not_3_out, not_4_out,
       not_5_out, xor_1_out, xor_2_out;

  not not_1 (not_1_out, en);
  and and_1 (and_1_out, not_1_out, not_2_out);
  not not_2 (not_2_out, c_prime_1);
  not not_3 (not_3_out, c_prime_0);
  xor xor_1 (xor_1_out, en, c_prime_1);
  and and_2 (and_2_out, and_1_out, not_4_out);
  not not_4 (not_4_out, c_prime_0);
  and and_3 (and_3_out, not_3_out, xor_1_out);
  and and_4 (and_4_out, c_prime_0, and_5_out);
  and and_5 (and_5_out, en, not_5_out);
  not not_5 (not_5_out, c_prime_1);
  xor xor_2 (xor_2_out, and_2_out, and_4_out);
  D_Flip_Flop d_ff_1 (.clk(clk), .D(and_3_out), .Q(c_prime_0));  // open: Qn, preset, en, reset
  D_Flip_Flop d_ff_2 (.clk(clk), .D(xor_2_out), .Q(c_prime_1));  // open: Qn, preset, en, reset
endmodule

module q01_05 (
  input  clk,
  input  en,
  output c_prime_0,
  output c_prime_1,
  output carry
);

  wire and_1_out, and_2_out, and_3_out, and_4_out, d_ff_1_q, not_1_out, not_2_out, not_3_out, xor_1_out;

  xor xor_1 (xor_1_out, c_prime_0, en);
  not not_1 (not_1_out, c_prime_1);
  and and_1 (and_1_out, xor_1_out, not_1_out);
  not not_2 (not_2_out, c_prime_1);
  and and_2 (and_2_out, not_2_out, c_prime_0);
  and and_3 (and_3_out, and_2_out, en);
  D_Flip_Flop d_ff_1 (.clk(clk), .D(en), .Q(d_ff_1_q));  // open: Qn, preset, en, reset
  D_Flip_Flop d_ff_2 (.clk(clk), .D(and_1_out), .Q(c_prime_0));  // open: Qn, preset, en, reset
  D_Flip_Flop d_ff_3 (.clk(clk), .D(and_3_out), .Q(c_prime_1));  // open: Qn, preset, en, reset
  not not_3 (not_3_out, c_prime_0);
  and and_4 (and_4_out, c_prime_1, not_3_out);
  and and_5 (carry, and_4_out, d_ff_1_q);
endmodule
