// Logisim project e_q2_00.circ as structural Verilog
// HA
module Half_Adder (
  input  A,
  input  B,
  output S,
  output C
);

  wire not_1_out, or_1_out;

  or or_1 (or_1_out, A, B);
  and and_1 (C, A, B);
  not not_1 (not_1_out, C);
  and and_2 (S, or_1_out, not_1_out);
endmodule

module Full_Adder (
  input  A,
  input  B,
  input  X,
  output S,
  output C
);

  wire half_adder_1_c, half_adder_1_s, half_adder_2_c;

  Half_Adder half_adder_1 (.A(A), .B(B), .S(half_adder_1_s), .C(half_adder_1_c));
  Half_Adder half_adder_2 (.A(half_adder_1_s), .B(X), .S(S), .C(half_adder_2_c));
  or or_1 (C, half_adder_2_c, half_adder_1_c);
endmodule

module Subtraction_n_bit (
  input  [3:0] A,
  input  [3:0] B,
  output [3:0] S
);

  wire [3:0] not_1_out;

  assign not_1_out = ~B;  // NOT_Gate not_1, 4 bits wide
  Adder #(.width(4)) adder_1 (.a(A), .b(not_1_out), .out(S), .cin(1'b1));  // open: cout

  // Notes on the sheet:
  //   n-bit adder
endmodule

module Add_Subb_n_bit (
  input  F,
  input  [3:0] A,
  input  [3:0] B,
  output [3:0] S
);

  wire [3:0] bit_extender_1_out, xor_1_out;

  assign bit_extender_1_out = {{3{F}}, F};  // Bit_Extender bit_extender_1
  assign xor_1_out = B ^ bit_extender_1_out;  // XOR_Gate xor_1, 4 bits wide
  Adder #(.width(4)) adder_1 (.a(A), .b(xor_1_out), .out(S), .cin(F));  // open: cout

  // Notes on the sheet:
  //   n-bit adder
endmodule
