// Logisim project e_q02_00.circ as structural Verilog
module P3 (
  input  In0,
  input  In1,
  input  In2,
  output Out0,
  output Out1
);

  wire and_1_out, and_2_out, xor_1_out;

  xor xor_1 (xor_1_out, In0, In1);
  and and_1 (and_1_out, In0, In1);
  and and_2 (and_2_out, xor_1_out, In2);
  xor xor_2 (Out0, xor_1_out, In2);
  or or_1 (Out1, and_1_out, and_2_out);
endmodule

module XOR (
  input  in_1,
  input  in_2,
  output out_3
);

  wire and_1_out, not_1_out, or_1_out;

  or or_1 (or_1_out, in_1, in_2);
  and and_1 (and_1_out, in_1, in_2);
  and and_2 (out_3, or_1_out, not_1_out);
  not not_1 (not_1_out, and_1_out);
endmodule

module P6 (
  input  In0,
  input  In1,
  input  In2,
  input  In4,
  input  In5,
  input  In6,
  output Out0,
  output Out1,
  output Out2
);

  wire and_1_out, p3_1_out0, p3_1_out1, p3_2_out0, p3_2_out1, xor_2_out;

  P3 p3_1 (.In0(In0), .In1(In1), .In2(In2), .Out0(p3_1_out0), .Out1(p3_1_out1));
  P3 p3_2 (.In0(In4), .In1(In5), .In2(In6), .Out0(p3_2_out0), .Out1(p3_2_out1));
  xor xor_1 (Out0, p3_1_out0, p3_2_out0);
  xor xor_2 (xor_2_out, p3_1_out1, p3_2_out1);
  and and_1 (and_1_out, p3_1_out0, p3_2_out0);
  and and_2 (Out2, p3_1_out1, p3_2_out1);
  xor xor_3 (Out1, xor_2_out, and_1_out);
endmodule
