// Logisim project e_q02.circ as structural Verilog
module Q2_2 (
  input  addr_low,
  input  d00,
  input  d01,
  input  d10,
  input  d11,
  input  addr_high,
  output \output 
);

  wire clk_out, d_ff_1_q, d_ff_2_q, d_ff_3_q, d_ff_4_q, multiplexer_1_out, multiplexer_2_out;

  Clock clk (.out(clk_out));
  D_Flip_Flop d_ff_1 (.clk(clk_out), .D(d00), .Q(d_ff_1_q));  // open: Qn, preset, en, reset
  D_Flip_Flop d_ff_2 (.clk(clk_out), .D(d01), .Q(d_ff_2_q));  // open: Qn, preset, en, reset
  D_Flip_Flop d_ff_3 (.clk(clk_out), .D(d10), .Q(d_ff_3_q));  // open: Qn, preset, en, reset
  D_Flip_Flop d_ff_4 (.clk(clk_out), .D(d11), .Q(d_ff_4_q));  // open: Qn, preset, en, reset
  Multiplexer multiplexer_1 (.in0(d_ff_1_q), .in1(d_ff_2_q), .out(multiplexer_1_out), .sel(addr_low));  // open: en
  Multiplexer multiplexer_2 (.in0(d_ff_3_q), .in1(d_ff_4_q), .out(multiplexer_2_out), .sel(addr_low));  // open: en
  Multiplexer multiplexer_3 (
    .in0(multiplexer_1_out), .in1(multiplexer_2_out), .out(\output ), .sel(addr_high));  // open: en
endmodule

module Q2_4 (
  input  we,
  input  d,
  input  we_2,
  input  d_2,
  output \output ,
  output output_2
);

  wire clk_2_out, clk_out, d_ff_1_q, d_ff_2_q, multiplexer_1_out;

  Clock clk (.out(clk_out));
  D_Flip_Flop d_ff_1 (.clk(clk_out), .D(d), .Q(d_ff_1_q));  // open: Qn, preset, en, reset
  Clock clk_2 (.out(clk_2_out));
  Multiplexer #(.enable("false")) multiplexer_1 (.in0(\output ), .in1(d_ff_1_q), .out(multiplexer_1_out), .sel(we));
  D_Flip_Flop d_ff_2 (.clk(clk_2_out), .D(d_2), .Q(d_ff_2_q));  // open: Qn, preset, en, reset
  D_Flip_Flop d_ff_3 (.clk(clk_out), .D(multiplexer_1_out), .Q(\output ));  // open: Qn, preset, en, reset
  Multiplexer #(.enable("false")) multiplexer_2 (.in0(output_2), .in1(d_ff_2_q), .out(output_2), .sel(we_2));
endmodule

module Q2_5 (
  input  \input ,
  input  addr_low,
  input  addr_high
);

  wire _00_q, _01_q, _10_q, _11_q, and_1_out, and_2_out, and_3_out, and_4_out, clk_out, not_1_out, not_2_out;

  Clock clk (.out(clk_out));
  not not_1 (not_1_out, addr_low);
  not not_2 (not_2_out, addr_high);
  and and_1 (and_1_out, not_1_out, not_2_out);
  D_Flip_Flop _00 (.clk(clk_out), .D(\input ), .Q(_00_q), .en(and_1_out));  // open: Qn, preset, reset
  and and_2 (and_2_out, addr_low, not_2_out);
  D_Flip_Flop _01 (.clk(clk_out), .D(\input ), .Q(_01_q), .en(and_2_out));  // open: Qn, preset, reset
  and and_3 (and_3_out, not_1_out, addr_high);
  D_Flip_Flop _10 (.clk(clk_out), .D(\input ), .Q(_10_q), .en(and_3_out));  // open: Qn, preset, reset
  and and_4 (and_4_out, addr_low, addr_high);
  D_Flip_Flop _11 (.clk(clk_out), .D(\input ), .Q(_11_q), .en(and_4_out));  // open: Qn, preset, reset
endmodule
